# Fritzing sketch Schematic (saved by Fritzing 0.9.1b)
stripboards: 1
perfboards: 1

parts:
  Part1 = Arduino Uno (Rev3)  # not connected
  Part2 = Arduino ProtoShield
  J1 = Power Jack [package=power_jack_pth_lock]
  U1 = 3.5mm Audio Jack [package=audio-jack-3.5mm-smd]
  U2 = 3.5mm Audio Jack [package=audio-jack-3.5mm-smd]
  U3 = 3.5mm Audio Jack [package=audio-jack-3.5mm-smd]
  Part5 = EasyDriver_v44
  POT1 = Analog Thumb Joystick
  LCD2 = Adafruit Negative RGB 2x16 LCD  # not connected
  M1 = Stepper Motor - Bipolar
  Q1 = PNP-Transistor [package="TO92 [THT]"]
  R1 = Resistor [tolerance=±5% resistance=330 package=THT]
  R2 = Resistor [tolerance=±5% resistance=10k package=THT]
  R3 = Resistor [tolerance=±5% resistance=10k package=THT]
  R4 = Resistor [tolerance=±5% resistance=10k package=THT]

nets:
  5V: Part2.5V, U1.RIGHT, U3.RIGHT, POT1.Vcc
  GND: Part2.GND, Part2.VIN, Part2.D4, Part2.D6, Part2.D10, Part2.N$57, Part2.N$145, Part2.N$167, Part2.N$178, J1.PWR, U2.SLEEVE, Part5.GND, POT1.GND, Q1.E, R2.Pin_0, R3.Pin_0, R4.Pin_0
  N1: Part2.D2, Part5.DIR
  N2: Part2.D3, Part5.STEP
  N3: Part2.D7, Part2.N$14, R1.Pin_1
  N4: Part2.A1, POT1.Yout
  N5: Part2.A0, POT1.Xout
  N6: Part2.D9, Part5.ENABLE
  N7: Part2.N$58, Q1.B, R1.Pin_0
  N8: Part2.N$59, U2.RIGHT, Q1.C
  N9: Part2.N$149, U1.LEFT, R4.Pin_1
  N10: Part2.N$171, U3.LEFT, R3.Pin_1
  N11: Part2.N$182, POT1.Select, R2.Pin_1
  N12: J1.GND, Part5.V+
  N13: Part5.OUT2A, M1.A
  N14: Part5.OUT2B, M1.C
  N15: Part5.OUT1A, M1.B
  N16: Part5.OUT1B, M1.D

notes:
  <- Adafruit spi backpack
  Green -> DAT
  Yellow -> CLK
  Red -> 5V
  Black -> GND
  Polou Step Up Voltage Regulator ->
  Converts 12V input to ~30v, allowing stepper to generate maximum power.
  Should be Big Easy Driver ->
  Current Adjustment @ ~40%
  12v AC Input->
  <- Camera Trigger. To trigger a canon t2i an adapter from 3.5mm to 2.5mm is necessary.
  <- End Switches
  Sense when slider is at the end of the track, one for each end.

custom parts:
  Adafruit Negative RGB 2x16 LCD: Adafruit Negative 2x16 LCD Display with RGB Backlight
